// Digital circuit ALU.dig as structural Verilog
module ALU (
  input  [31:0] A,
  input  [31:0] B,
  input  [1:0] OP_ALU,
  output [31:0] R,
  output [3:0] NZCV
);

  wire and_1_out, and_2_out;
  wire [31:0] add_1_s, sub_1_s;
  wire [63:0] mul_1_mul;

  Add #(.Bits(32)) add_1 (.a(A), .b(B), .c_i(1'b0), .s(add_1_s));  // open: c_o
  Sub #(.Bits(32)) sub_1 (.a(A), .b(B), .c_i(1'b0), .s(sub_1_s));  // open: c_o
  Mul #(.Bits(32)) mul_1 (.a(A), .b(B), .mul(mul_1_mul));
  Multiplexer #(.Selector_Bits(2), .Bits(32)) multiplexer_1 (
    .sel(OP_ALU), .in_0(add_1_s), .in_1(sub_1_s), .in_2(mul_1_mul[31:0]), .in_3({32{1'b0}}),
    .out({R[31:1], NZCV[0]}));
  Comparator #(.Bits(32)) comparator_1 (.a({R[31:1], NZCV[0]}), .b({32{1'b0}}), .eq(NZCV[1]));  // open: gt, lt
  Comparator #(.Bits(32)) comparator_2 (.a(A), .b(B), .gt(NZCV[2]));  // open: eq, lt
  and and_1 (and_1_out, ~A[31], B[31], R[31]);  // And
  and and_2 (and_2_out, A[31], ~B[31], ~R[31]);  // And
  or or_1 (NZCV[3], and_1_out, and_2_out);

  assign R[0] = NZCV[0];
endmodule
