// Digital circuit DRIVER.dig as structural Verilog
module DRIVER (
  input  clk,
  input  [2:0] in_2
);

  wire a_mul, ALU1src, ALUop, and_1_out, B, BL, BX, C, control_unit_conditional_1_p2, dipswitch_1_out,
       FINISHED__GREEN_eq, i_dp, MOV, MR, MUL, MW, N, r0, r1, r2, r3, r4, r5, r6, r7, r8, r9, r10, r11, r12,
       r13, r14, r15, register_file_1_p8, RFW, V, Z;
  wire [1:0] EXT;
  wire [3:0] cond, multiplexer_3_out, multiplexer_4_out, multiplexer_5_out, multiplexer_6_out,
       multiplexer_7_out;
  wire [23:0] b_offset;
  wire [27:24] iw;
  wire [31:0] add_1_s, add_2_s, ALU_p4, extension_unit_1_extimm, multiplexer_2_out, multiplexer_8_out,
       multiplexer_9_out, multiplexer_10_out, pc_in, pc_out, ramdualport_1_d, register_file_1_p9;

  // Probe on r0
  // Probe on r1
  // Probe on r2
  // Probe on r3
  // Probe on r4
  // Probe on r5
  // Probe on r6
  // Probe on r7
  // Probe on r8
  // Probe on r9
  // Probe on r10
  // Probe on r11
  // Probe on r12
  // Probe on r13
  // Probe on r14
  // Probe on r15
  // Probe on pc_out
  DipSwitch dipswitch_1 (.out(dipswitch_1_out));
  // Probe on N
  // Probe on Z
  // Probe on C
  // Probe on V
  and and_1 (and_1_out, clk, dipswitch_1_out);
  Multiplexer #(.Bits(32)) multiplexer_1 (.sel(BX), .in_0(multiplexer_2_out), .in_1(register_file_1_p9), .out(pc_in));
  Multiplexer #(.Bits(32)) multiplexer_2 (.sel(B), .in_0(add_1_s), .in_1(multiplexer_10_out), .out(multiplexer_2_out));
  Comparator #(.Bits(32)) FINISHED__GREEN (.a(pc_in), .b(pc_out), .eq(FINISHED__GREEN_eq));  // open: gt, lt
  Register #(.Bits(32)) PC (.D(pc_in), .C(and_1_out), .en(1'b1), .Q(pc_out));
  LED led_1 (.in(FINISHED__GREEN_eq));
  Add #(.Bits(32)) add_1 (.a(pc_out), .b(32'h4), .c_i(1'b0), .s(add_1_s));  // open: c_o
  instruction_memory instruction_memory_1 (
    .A(pc_out[7:2]), .PN(in_2), .D({cond, iw[27:26], i_dp, iw[24], b_offset[23:22], a_mul, b_offset[20:0]}));
  // control_unit_conditional control_unit_conditional_1: pin names not known; wires that end beside it: {cond, iw[27:26], i_dp, iw[24], b_offset[23:22], a_mul, b_offset[20:0]}, control_unit_conditional_1_p2, and_1_out, RFW, EXT, ALUop, ALU1src, B, BL, BX, MUL, MOV, MR, MW
  // Probe on {cond, iw[27:26], i_dp, iw[24], b_offset[23:22], a_mul, b_offset[20:0]}
  Add #(.Bits(32)) add_2 (.a(add_1_s), .b(32'h4), .c_i(1'b0), .s(add_2_s));  // open: c_o
  Multiplexer #(.Bits(4)) multiplexer_3 (
    .sel(MUL), .in_0(b_offset[19:16]), .in_1(b_offset[11:8]), .out(multiplexer_3_out));
  Multiplexer #(.Bits(4)) multiplexer_4 (
    .sel(MUL), .in_0(b_offset[15:12]), .in_1(b_offset[19:16]), .out(multiplexer_4_out));
  Multiplexer #(.Bits(4)) multiplexer_5 (.sel(B), .in_0(multiplexer_3_out), .in_1(4'b1111), .out(multiplexer_5_out));
  Multiplexer #(.Bits(4)) multiplexer_6 (
    .sel(MW), .in_0(b_offset[3:0]), .in_1(multiplexer_4_out), .out(multiplexer_6_out));
  // Probe on pc_in
  // Probe on pc_out
  Multiplexer #(.Bits(4)) multiplexer_7 (.sel(BL), .in_0(multiplexer_4_out), .in_1(4'b1110), .out(multiplexer_7_out));
  Multiplexer #(.Bits(32)) multiplexer_8 (.sel(BL), .in_0(multiplexer_10_out), .in_1(add_1_s), .out(multiplexer_8_out));
  // Register_File register_file_1: pin names not known; wires that end beside it: multiplexer_5_out, multiplexer_6_out, and_1_out, multiplexer_7_out, multiplexer_8_out, add_2_s, RFW, register_file_1_p8, register_file_1_p9, r0, r1, r2, r3, r4, r5, r6, r7, r8, r9, r10, r11, r12, r13, r14, r15
  Extension_Unit extension_unit_1 (
    .iw({cond, iw[27:26], i_dp, iw[24], b_offset[23:22], a_mul, b_offset[20:0]}), .EXT(EXT),
    .extimm(extension_unit_1_extimm));
  Multiplexer #(.Bits(32)) multiplexer_9 (
    .sel(ALU1src), .in_0(register_file_1_p9), .in_1(extension_unit_1_extimm), .out(multiplexer_9_out));
  // Probe on extension_unit_1_extimm
  // alu_gdb ALU: pin names not known; wires that end beside it: register_file_1_p8, multiplexer_9_out, ALUop, ALU_p4, control_unit_conditional_1_p2, N, Z, C, V
  Multiplexer #(.Bits(32)) multiplexer_10 (.sel(MR), .in_0(ALU_p4), .in_1(ramdualport_1_d), .out(multiplexer_10_out));
  RAMDualPort #(.AddrBits(9), .Bits(32)) ramdualport_1 (
    .A(ALU_p4[10:2]), .Din(register_file_1_p9), .str(MW), .C(and_1_out), .ld(MR), .D(ramdualport_1_d));

  // Other names for the same wires on the sheet: imm[7:0] = b_offset[7:0]; immoff[11:0] = b_offset[11:0];
  //   iw (some bits) = {cond, i_dp, b_offset[23:22], a_mul, b_offset[20:0]}; rm[3:0] = b_offset[3:0];
  //   rm_mul[3:0] = b_offset[3:0]; opmul4[3:0] = b_offset[7:4]; rs_mul[3:0] = b_offset[11:8];
  //   rd[3:0] = b_offset[15:12]; rn_mul[3:0] = b_offset[15:12]; rd_mul[3:0] = b_offset[19:16];
  //   rn[3:0] = b_offset[19:16]; l_sdt = b_offset[20]; s_dp = b_offset[20]; s_mul = b_offset[20];
  //   b_offset[21] = a_mul; opc[3:0] = {iw[24], b_offset[23:22], a_mul}; w_sdt = a_mul; b_sdt = b_offset[22];
  //   opmul6[5:0] = {iw[27:26], i_dp, iw[24], b_offset[23:22]}; u_sdt = b_offset[23]; l_b = iw[24]; p_sdt = iw[24];
  //   i_sdt = i_dp; opb3[2:0] = {iw[27:26], i_dp}; op2[1:0] = iw[27:26]; opmul2[1:0] = iw[27:26]

  // Notes on the sheet:
  //   clk: Hz: 2147483647
endmodule
