// Digital circuit Decoder.dig as structural Verilog
module Decoder (
  input  [3:0] SEL,
  input  EN,
  output Out_0,
  output Out_1,
  output Out_2,
  output Out_3,
  output Out_4,
  output Out_5,
  output Out_6,
  output Out_7,
  output Out_8,
  output Out_9,
  output Out_10,
  output Out_11,
  output Out_12,
  output Out_13,
  output Out_14,
  output Out_15
);

  wire decoder_1_out_0, decoder_1_out_1, decoder_1_out_2, decoder_1_out_3, decoder_1_out_4, decoder_1_out_5,
       decoder_1_out_6, decoder_1_out_7, decoder_1_out_8, decoder_1_out_9, decoder_1_out_10,
       decoder_1_out_11, decoder_1_out_12, decoder_1_out_13, decoder_1_out_14, decoder_1_out_15;

  Decoder #(.Selector_Bits(4)) decoder_1 (
    .sel(SEL), .out_0(decoder_1_out_0), .out_1(decoder_1_out_1), .out_2(decoder_1_out_2),
    .out_3(decoder_1_out_3), .out_4(decoder_1_out_4), .out_5(decoder_1_out_5), .out_6(decoder_1_out_6),
    .out_7(decoder_1_out_7), .out_8(decoder_1_out_8), .out_9(decoder_1_out_9), .out_10(decoder_1_out_10),
    .out_11(decoder_1_out_11), .out_12(decoder_1_out_12), .out_13(decoder_1_out_13),
    .out_14(decoder_1_out_14), .out_15(decoder_1_out_15));
  and and_1 (Out_0, EN, decoder_1_out_0);
  and and_2 (Out_1, EN, decoder_1_out_1);
  and and_3 (Out_2, EN, decoder_1_out_2);
  and and_4 (Out_3, EN, decoder_1_out_3);
  and and_5 (Out_4, EN, decoder_1_out_4);
  and and_6 (Out_5, EN, decoder_1_out_5);
  and and_7 (Out_6, EN, decoder_1_out_6);
  and and_8 (Out_7, EN, decoder_1_out_7);
  and and_9 (Out_8, EN, decoder_1_out_8);
  and and_10 (Out_9, EN, decoder_1_out_9);
  and and_11 (Out_10, EN, decoder_1_out_10);
  and and_12 (Out_11, EN, decoder_1_out_11);
  and and_13 (Out_12, EN, decoder_1_out_12);
  and and_14 (Out_13, EN, decoder_1_out_13);
  and and_15 (Out_14, EN, decoder_1_out_14);
  and and_16 (Out_15, EN, decoder_1_out_15);
endmodule
