// Digital circuit Extension Unit.dig as structural Verilog
module Extension_Unit (
  input  [31:0] iw,
  input  [1:0] EXT,
  output [31:0] extimm
);

  wire [31:0] bitextender_1_out;
  wire [63:0] mul_1_mul;

  BitExtender #(.inputBits(24), .outputBits(32)) bitextender_1 (.in(iw[23:0]), .out(bitextender_1_out));
  Mul #(.Bits(32)) mul_1 (.a(bitextender_1_out), .b(32'h4), .mul(mul_1_mul));
  Multiplexer #(.Selector_Bits(2), .Bits(32)) multiplexer_1 (
    .sel(EXT), .in_0({{24{1'b0}}, iw[7:0]}), .in_1({{20{1'b0}}, iw[11:0]}), .in_2(mul_1_mul[31:0]),
    .in_3({32{1'b0}}), .out(extimm));

  // Notes on the sheet:
  //   EXT: 1 for 8 bit
  //   2 for 12 bit
  //   3 for 24 bit
endmodule
