// Digital circuit Register File.dig as structural Verilog
module Register_File (
  input  [3:0] Write_Addr,
  input  [31:0] Write_Data,
  input  Write_Enable,
  input  CLK,
  input  [31:0] PC,
  input  [3:0] READ_R0,
  input  [3:0] READ_R1,
  output [31:0] RD0,
  output [31:0] RD1,
  output [31:0] R2,
  output [31:0] R3,
  output [31:0] R4,
  output [31:0] R5,
  output [31:0] R6,
  output [31:0] R7,
  output [31:0] R8,
  output [31:0] R9,
  output [31:0] R10,
  output [31:0] R11,
  output [31:0] R12,
  output [31:0] R13,
  output [31:0] R14,
  output [31:0] R15,
  output [31:0] R0,
  output [31:0] R1
);

  wire O0, O1, O2, O3, O4, O5, O6, O7, O8, O9, O10, O11, O12, O13, O14, O15;
  wire [31:0] Q15;

  // Decoder decoder_1: pin names not known; wires that end beside it: Write_Addr, Write_Enable, O0, O1, O2, O3, O4, O5, O6, O7, O8, O9, O10, O11, O12, O13, O14, O15
  Register #(.Bits(32)) register_1 (.D(Write_Data), .C(CLK), .en(O0), .Q(R0));
  Register #(.Bits(32)) register_2 (.D(Write_Data), .C(CLK), .en(O1), .Q(R1));
  Register #(.Bits(32)) register_3 (.D(Write_Data), .C(CLK), .en(O2), .Q(R2));
  Register #(.Bits(32)) register_4 (.D(Write_Data), .C(CLK), .en(O3), .Q(R3));
  Register #(.Bits(32)) register_5 (.D(Write_Data), .C(CLK), .en(O4), .Q(R4));
  Register #(.Bits(32)) register_6 (.D(Write_Data), .C(CLK), .en(O5), .Q(R5));
  Register #(.Bits(32)) register_7 (.D(Write_Data), .C(CLK), .en(O6), .Q(R6));
  Register #(.Bits(32)) register_8 (.D(Write_Data), .C(CLK), .en(O7), .Q(R7));
  Register #(.Bits(32)) register_9 (.D(Write_Data), .C(CLK), .en(O8), .Q(R8));
  Register #(.Bits(32)) register_10 (.D(Write_Data), .C(CLK), .en(O9), .Q(R9));
  Register #(.Bits(32)) register_11 (.D(Write_Data), .C(CLK), .en(O10), .Q(R10));
  Register #(.Bits(32)) register_12 (.D(Write_Data), .C(CLK), .en(O11), .Q(R11));
  Register #(.Bits(32)) register_13 (.D(Write_Data), .C(CLK), .en(O12), .Q(R12));
  Register #(.Bits(32)) register_14 (.D(Write_Data), .C(CLK), .en(O13), .Q(R13));
  Register #(.Bits(32)) register_15 (.D(Write_Data), .C(CLK), .en(O14), .Q(R14));
  Register #(.Bits(32)) register_16 (.D(Write_Data), .C(CLK), .en(O15), .Q(Q15));
  Multiplexer #(.Selector_Bits(4), .Bits(32)) multiplexer_1 (
    .sel(READ_R1), .in_0(R0), .in_1(R1), .in_2(R2), .in_3(R3), .in_4(R4), .in_5(R5), .in_6(R6), .in_7(R7),
    .in_8(R8), .in_9(R9), .in_10(R10), .in_11(R11), .in_12(R12), .in_13(R13), .in_14(R14), .in_15(PC),
    .out(RD1));
  Multiplexer #(.Selector_Bits(4), .Bits(32)) multiplexer_2 (
    .sel(READ_R0), .in_0(R0), .in_1(R1), .in_2(R2), .in_3(R3), .in_4(R4), .in_5(R5), .in_6(R6), .in_7(R7),
    .in_8(R8), .in_9(R9), .in_10(R10), .in_11(R11), .in_12(R12), .in_13(R13), .in_14(R14), .in_15(PC),
    .out(RD0));

  assign R15 = PC;

  // Other names for the same wires on the sheet: C = CLK; Q0[31:0] = R0; Q1[31:0] = R1; Q2[31:0] = R2; Q3[31:0] = R3;
  //   Q4[31:0] = R4; Q5[31:0] = R5; Q6[31:0] = R6; Q7[31:0] = R7; Q8[31:0] = R8; Q9[31:0] = R9; Q10[31:0] = R10;
  //   Q11[31:0] = R11; Q12[31:0] = R12; Q13[31:0] = R13; Q14[31:0] = R14
endmodule
