// Digital circuit control_unit_2.dig as structural Verilog
module control_unit_2 (
  input  [31:0] iw,
  output RFW,
  output [1:0] EXT,
  output [1:0] ALUop,
  output BR,
  output ALU1src,
  output BL,
  output BX,
  output cmp
);

  wire add_i, add_r, cmp_t, comparator_1_eq, comparator_2_eq, comparator_3_eq, mov_i, or_1_out, or_2_out,
       or_3_out, or_4_out;

  // Probe on iw
  Comparator #(.Bits(4)) comparator_1 (.a(iw[24:21]), .b(4'b0100), .eq(comparator_1_eq));  // open: gt, lt
  Comparator #(.Bits(4)) comparator_2 (.a(iw[24:21]), .b(4'b1101), .eq(comparator_2_eq));  // open: gt, lt
  Comparator #(.Bits(4)) comparator_3 (.a(iw[24:21]), .b(4'b1010), .eq(comparator_3_eq));  // open: gt, lt
  and and_1 (add_r, ~iw[27], ~iw[26], ~iw[25], comparator_1_eq);  // And
  and and_2 (add_i, ~iw[27], ~iw[26], iw[25], comparator_1_eq);  // And
  and and_3 (mov_i, ~iw[27], ~iw[26], iw[25], comparator_2_eq);  // And
  and and_4 (cmp_t, ~iw[27], ~iw[26], iw[25], comparator_3_eq);  // And
  and and_5 (BR, iw[27], ~iw[26], iw[25]);  // And
  and and_6 (BL, BR, iw[24]);
  Comparator #(.Bits(24)) comparator_4 (.a(iw[27:4]), .b(24'h12fff1), .eq(BX));  // open: gt, lt
  or or_1 (or_1_out, add_r, add_i, mov_i);
  or or_2 (or_2_out, add_i, mov_i);
  or or_3 (or_3_out, add_i, mov_i);
  or or_4 (or_4_out, add_i, mov_i, BR);
  or or_5 (RFW, or_1_out, 1'b0);
  or or_6 (EXT[0], 1'b0, 1'b0);
  or or_7 (EXT[1], BR, 1'b0);
  or or_8 (ALUop[0], or_2_out, 1'b0);
  or or_9 (ALUop[1], or_3_out, 1'b0);
  or or_10 (ALU1src, or_4_out, 1'b0);

  assign cmp = BR;

  // Other names for the same wires on the sheet: b_offset[23:0] = iw[23:0]; imm[7:0] = iw[7:0];
  //   immoff[11:0] = iw[11:0]; rm[3:0] = iw[3:0]; rm_mul[3:0] = iw[3:0]; bxcode[23:0] = iw[27:4];
  //   opmul4[3:0] = iw[7:4]; rs_mul[3:0] = iw[11:8]; rd[3:0] = iw[15:12]; rn_mul[3:0] = iw[15:12];
  //   rd_mul[3:0] = iw[19:16]; rn[3:0] = iw[19:16]; l_sdt = iw[20]; s_dp = iw[20]; s_mul = iw[20]; a_mul = iw[21];
  //   opc[3:0] = iw[24:21]; w_sdt = iw[21]; b_sdt = iw[22]; opmul6[4:0] = iw[27:23]; u_sdt = iw[23]; l_b = iw[24];
  //   p_sdt = iw[24]; i_sdt = iw[25]; op0 = iw[25]; op0_i_dp = iw[25]; op1 = iw[26]; opmul2[1:0] = iw[27:26];
  //   op2 = iw[27]; cond[3:0] = iw[31:28]

  // Notes on the sheet:
  //   add(r)
  //   add(i)
  //   mov(i)
  //   b
  //   bl
endmodule
