// Digital circuit control_unit_conditional.dig as structural Verilog
module control_unit_conditional (
  input  [31:0] iw,
  input  [3:0] NZCV,
  input  CLK,
  output RFW,
  output [1:0] EXT,
  output [1:0] ALUop,
  output ALU1src,
  output B,
  output BL,
  output BX,
  output MUL,
  output MOV,
  output MR,
  output MW
);

  wire AL_eq, and_1_out, and_2_out, and_3_out, and_4_out, and_6_out, C, EQ_eq, GT_eq, LE_eq, LT_eq,
       main_decoder_1_b, main_decoder_1_cmp, N, NE_eq, or_1_out, or_2_out, V, xnor_1_out, xor_1_out,
       xor_2_out, Z;

  main_decoder main_decoder_1 (
    .iw(iw), .RFW(RFW), .EXT(EXT), .ALUop(ALUop), .ALU1src(ALU1src), .B(main_decoder_1_b), .BL(BL), .BX(BX),
    .MUL(MUL), .MOV(MOV), .MR(MR), .MW(MW), .cmp(main_decoder_1_cmp));  // open: cmp_i
  Register #(.Bits(4)) register_1 (.D(NZCV), .C(CLK), .en(main_decoder_1_cmp), .Q({V, C, Z, N}));
  Comparator #(.Bits(4)) AL (.a(iw[31:28]), .b(4'b1110), .eq(AL_eq));  // open: gt, lt
  Comparator #(.Bits(4)) EQ (.a(iw[31:28]), .b(4'b0000), .eq(EQ_eq));  // open: gt, lt
  Comparator #(.Bits(4)) NE (.a(iw[31:28]), .b(4'b0001), .eq(NE_eq));  // open: gt, lt
  Comparator #(.Bits(4)) LT (.a(iw[31:28]), .b(4'b1011), .eq(LT_eq));  // open: gt, lt
  Comparator #(.Bits(4)) GT (.a(iw[31:28]), .b(4'b1100), .eq(GT_eq));  // open: gt, lt
  Comparator #(.Bits(4)) LE (.a(iw[31:28]), .b(4'b1101), .eq(LE_eq));  // open: gt, lt
  xnor xnor_1 (xnor_1_out, V, N);
  and and_1 (and_1_out, Z, EQ_eq);
  and and_2 (and_2_out, ~Z, NE_eq);  // And
  xor xor_1 (xor_1_out, V, N);
  and and_3 (and_3_out, LT_eq, xor_1_out);
  xor xor_2 (xor_2_out, N, V);
  and and_4 (and_4_out, GT_eq, xnor_1_out, ~Z);  // And
  or or_1 (or_1_out, AL_eq, and_1_out, and_2_out, and_3_out, and_4_out, and_6_out);
  or or_2 (or_2_out, Z, xor_2_out);
  and and_5 (B, main_decoder_1_b, or_1_out);
  and and_6 (and_6_out, LE_eq, or_2_out);
endmodule
