// Digital circuit instruction_memory.dig as structural Verilog
module instruction_memory (
  input  [5:0] A,
  input  [2:0] PN,
  output [31:0] D
);

  wire [31:0] Fib_Iter_19_d, Fib_Rec_19_d, Find_Max_d, rom_1_d, Sum_Array_d;

  ROM #(.AddrBits(6), .Bits(32)) Fib_Iter_19 (.A(A), .sel(1'b1), .D(Fib_Iter_19_d));
  ROM #(.AddrBits(6), .Bits(32)) Fib_Rec_19 (.A(A), .sel(1'b1), .D(Fib_Rec_19_d));
  ROM #(.AddrBits(6), .Bits(32)) Find_Max (.A(A), .sel(1'b1), .D(Find_Max_d));
  ROM #(.AddrBits(6), .Bits(32)) Sum_Array (.A(A), .sel(1'b1), .D(Sum_Array_d));
  ROM #(.AddrBits(6), .Bits(32)) rom_1 (.A(A), .sel(1'b1), .D(rom_1_d));
  Multiplexer #(.Selector_Bits(3), .Bits(32)) multiplexer_1 (
    .sel(PN), .in_0(Fib_Iter_19_d), .in_1(Fib_Rec_19_d), .in_2(Find_Max_d), .in_3(Sum_Array_d),
    .in_4(rom_1_d), .in_5({32{1'b0}}), .in_6({32{1'b0}}), .in_7({32{1'b0}}), .out(D));

  // Notes on the sheet:
  //   contents of Fib_Iter_19 (hex, n*v repeats v):
  //   e3a00013,eb000001,eaffffff,eafffffe,e3500000,3a02000,a00000c,e3a01000,e3a02001,e2400001,
  //   e3500000,a000007,eaffffff,e0813002,e1a01002,e1a02003,e2400001,e3500000,a000000,eafffff8,
  //   e1a00002,e12fff1e
  //   contents of Fib_Rec_19 (hex, n*v repeats v):
  //   e3a00013,eb000001,eaffffff,eafffffe,e24dd010,e3500000,a00000f,e3500001,1a000001,e3a00001,
  //   ea00000d,e58de000,e58d0004,e2400001,ebfffff4,e1a01000,e58d1008,e59d0004,e2400002,
  //   ebffffef,e59d1008,e59de000,e0810000,e28dd010,e12fff1e,e28dd010,e12fff1e
  //   contents of Find_Max (hex, n*v repeats v):
  //   e3a0d080,e24dd018,e3a0000c,e58d0000,e3a00004,e58d0004,e3a000be,e58d0008,e3a000c8,
  //   e58d000c,e3a00003,e58d0010,e1a0000d,e3a01005,eb000001,eaffffff,eafffffe,e590c000,
  //   e1a0200c,e2411001,e2800004,e2411001,e590c000,e15c0002,da000000,e1a0200c,e2800004,
  //   e3510000,cafffff7,e1a00002,e12fff1e
  //   contents of Sum_Array (hex, n*v repeats v):
  //   e3a0d080,e24dd018,e3a0000a,e58d0000,e3a00004,e58d0004,e3a0000c,e58d0008,e3a0000e,
  //   e58d000c,e3a00002,e58d0010,e1a0000d,e3a01005,eb000001,eaffffff,eafffffe,e3a0c000,
  //   e3a02000,e3510000,a000004,e2411001,e7903002,e083c00c,e2822004,eafffff8,e1a0000c,e12fff1e
  //   contents of rom_1 (hex, n*v repeats v):
  //   e3a0d080,e24dd00c,e3a00001,e58d0000,e3a00002,e58d0004,e3a00003,e58d0008,e1a0000d,
  //   e3a01003,eb000000,eafffffe,e3a02000,e3a03000,e1520001,a000004,e590c000,e083300c,e2822001,
  //   e2800004,eafffff8,e1a00003,e12fff1e
endmodule
