// Digital circuit main_decoder.dig as structural Verilog
module main_decoder (
  input  [31:0] iw,
  output RFW,
  output [1:0] EXT,
  output B,
  output ALU1src,
  output BL,
  output BX,
  output cmp,
  output MUL,
  output MOV,
  output [1:0] ALUop,
  output cmp_i,
  output MR,
  output MW
);

  wire add_i, add_r, comparator_1_eq, comparator_2_eq, comparator_3_eq, comparator_4_eq, comparator_6_eq,
       comparator_7_eq, ld, ldimm, ldreg, mov_i, mov_r, or_2_out, or_3_out, or_4_out, or_5_out, or_6_out,
       or_13_out, or_14_out, sdt, str, strimm, strreg, sub_i, sub_r;

  // Probe on iw
  Comparator #(.Bits(4)) comparator_1 (.a(iw[24:21]), .b(4'b0100), .eq(comparator_1_eq));  // open: gt, lt
  Comparator #(.Bits(4)) comparator_2 (.a(iw[24:21]), .b(4'b0010), .eq(comparator_2_eq));  // open: gt, lt
  Comparator #(.Bits(4)) comparator_3 (.a(iw[24:21]), .b(4'b1101), .eq(comparator_3_eq));  // open: gt, lt
  and and_1 (sdt, ~iw[27], iw[26]);  // And
  Comparator #(.Bits(4)) comparator_4 (.a(iw[24:21]), .b(4'b1010), .eq(comparator_4_eq));  // open: gt, lt
  and and_2 (add_r, ~iw[27], ~iw[26], ~iw[25], comparator_1_eq);  // And
  and and_3 (add_i, ~iw[27], ~iw[26], iw[25], comparator_1_eq);  // And
  and and_4 (sub_r, ~iw[27], ~iw[26], ~iw[25], comparator_2_eq);  // And
  and and_5 (sub_i, ~iw[27], ~iw[26], iw[25], comparator_2_eq);  // And
  and and_6 (mov_i, ~iw[27], ~iw[26], iw[25], comparator_3_eq);  // And
  and and_7 (mov_r, ~iw[27], ~iw[26], ~iw[25], comparator_3_eq);  // And
  and and_8 (ld, sdt, iw[20]);
  and and_9 (str, sdt, ~iw[20]);  // And
  and and_10 (cmp, ~iw[27], ~iw[26], iw[24], comparator_4_eq);  // And
  and and_11 (B, iw[27], ~iw[26], iw[25]);  // And
  and and_12 (BL, B, iw[24]);
  Comparator #(.Bits(24)) comparator_5 (.a(iw[27:4]), .b(24'h12fff1), .eq(BX));  // open: gt, lt
  and and_13 (ldimm, ld, ~iw[25]);  // And
  and and_14 (ldreg, ld, iw[25]);
  and and_15 (strimm, str, ~iw[25]);  // And
  and and_16 (strreg, str, iw[25]);
  and and_17 (cmp_i, cmp, iw[25]);
  or or_1 (MOV, mov_i, mov_r);
  Comparator #(.Bits(4)) comparator_6 (.a(iw[7:4]), .b(4'b1001), .eq(comparator_6_eq));  // open: gt, lt
  or or_2 (or_2_out, add_r, add_i, mov_i);
  or or_3 (or_3_out, sub_r, sub_i, mov_r);
  or or_4 (or_4_out, add_i, mov_i, B, sub_i);
  or or_5 (or_5_out, cmp_i, ldimm, strimm, 1'b0);
  or or_6 (or_6_out, or_2_out, MUL, or_3_out, BL);
  Comparator #(.Bits(6)) comparator_7 (.a(iw[27:22]), .b({6{1'b0}}), .eq(comparator_7_eq));  // open: gt, lt
  or or_7 (EXT[0], ldimm, strimm);
  or or_8 (EXT[1], B, 1'b0);
  or or_9 (ALU1src, or_4_out, or_5_out, 1'b0);
  and and_18 (MUL, comparator_6_eq, comparator_7_eq);
  or or_10 (RFW, or_6_out, ldimm, ldreg);
  or or_11 (MR, ldimm, ldreg);
  or or_12 (MW, strimm, strreg);
  or or_13 (or_13_out, sub_r, sub_i);
  or or_14 (or_14_out, mov_r, mov_i);
  or or_15 (ALUop[0], or_13_out, cmp, cmp_i, or_14_out);
  or or_16 (ALUop[1], MUL, or_14_out);

  // Other names for the same wires on the sheet: b_offset[23:0] = iw[23:0]; imm[7:0] = iw[7:0];
  //   immoff[11:0] = iw[11:0]; rm[3:0] = iw[3:0]; rm_mul[3:0] = iw[3:0]; bxcode[23:0] = iw[27:4];
  //   opmul4[3:0] = iw[7:4]; rs_mul[3:0] = iw[11:8]; rd[3:0] = iw[15:12]; rn_mul[3:0] = iw[15:12];
  //   rd_mul[3:0] = iw[19:16]; rn[3:0] = iw[19:16]; l_sdt = iw[20]; s_dp = iw[20]; s_mul = iw[20]; a_mul = iw[21];
  //   opc[3:0] = iw[24:21]; w_sdt = iw[21]; b_sdt = iw[22]; opmul6[5:0] = iw[27:22]; u_sdt = iw[23]; l_b = iw[24];
  //   p_sdt = iw[24]; i_sdt = iw[25]; op0 = iw[25]; op0_i_dp = iw[25]; op1 = iw[26]; opmul2[1:0] = iw[27:26];
  //   op2 = iw[27]; cond[3:0] = iw[31:28]

  // Notes on the sheet:
  //   add(r)
  //   add(i)
  //   sub(r)
  //   sub(i)
  //   mov(i)
  //   mov(r)
  //   SDT
  //   b
  //   bl
  //   LOAD
  //   STORE
  //   LOAD w/ IMM
  //   LOAD w/ REG
  //   STR w/ IMM
  //   STR w/ REG
  //   mul
endmodule
